# Fritzing sketch circuit (saved by Fritzing 0.9.3b)
breadboards: 1

parts:
  Driver1 = 28BYJ-48 Driver Module [part_number=ULN2003 package=THT]
  SM1 = 28BYJ-48 Stepper Motor [part_number=28BYJ-48]
  Arduino = Arduino Uno (Rev3)
  BAT1 = BC9VPC [package=bc9vpc]
  LED1 = LED - 3mm [color="Green (565nm)" package="3 mm [THT]"]
  LED2 = LED - 3mm [color="Red (633nm)" package="3 mm [THT]"]
  LED3 = LED - 3mm [color="Yellow (592nm)" package="3 mm [THT]"]
  LED4 = LED - 3mm [color="Blue (430nm)" package="3 mm [THT]"]
  LED5 = LED - 3mm [color="Red (633nm)" package="3 mm [THT]"]
  LED6 = LED - 3mm [color="Green (565nm)" package="3 mm [THT]"]
  R1 = Resistor [tolerance=±5% resistance=220 package="0402 [SMD]"]
  R2 = Resistor [tolerance=±5% resistance=220 package="0402 [SMD]"]
  R3 = Resistor [tolerance=±5% resistance=220 package="0402 [SMD]"]
  R4 = Resistor [tolerance=±5% resistance=220 package="0402 [SMD]"]
  R5 = Resistor [tolerance=±5% resistance=220 package="0402 [SMD]"]
  R6 = Resistor [tolerance=±5% resistance=220 package="0402 [SMD]"]
  R7 = Trimmer Potentiometer [maximum_resistance=10kΩ package=THT]
  R8 = Trimmer Potentiometer [maximum_resistance=10kΩ package=THT]

nets:
  N1: Driver1.IN1, Arduino.D11_PWM/MOSI
  N2: Driver1.IN2, Arduino.D10_PWM/SS
  N3: Driver1.IN3, Arduino.D9_PWM
  N4: Driver1.IN4, Arduino.D8
  N5: Driver1.GND, BAT1.V-
  N6: Driver1.Vmotor, BAT1.V+
  N7: Driver1.blue-pin, SM1.blue-pin
  N8: Driver1.pink-pin, SM1.pink-pin
  N9: Driver1.yellow-pin, SM1.yellow-pin
  N10: Driver1.orange-pin, SM1.orange-pin
  N11: Driver1.red-pin, SM1.red-pin
  N12: Arduino.A0, R7.wiper
  N13: Arduino.A1, R8.wiper
  N14: Arduino.GND, R7.leg1, R8.leg1
  N15: Arduino.5V, R7.leg2, R8.leg2
  N16: LED1.cathode, LED2.cathode, LED3.cathode, LED4.cathode, LED5.cathode, LED6.cathode
  N17: LED1.anode, R1.Pin_0
  N18: LED2.anode, R2.Pin_0
  N19: LED3.anode, R3.Pin_0
  N20: LED4.anode, R4.Pin_0
  N21: LED5.anode, R5.Pin_0
  N22: LED6.anode, R6.Pin_0

custom parts:
  28BYJ-48 Driver Module: Generic male header
  28BYJ-48 Stepper Motor: Unipolar Stepper Motor 28BYJ-48 Top coil - pink & orange Bottom coil - blue & yellow Common rail - red Connector pins: blue - pink - yellow - orange - red
